# Fritzing sketch board_layout (saved by Fritzing 0.9.3b)
circuit board: 10cm x 6cm
perfboards: 1

parts:
  C2 = Capacitor [package=cap-pth-small2]
  U1 = atmega328 [package=dip]
  XTAL1 = Crystal [frequency="16 Mhz" package=THT]
  C1 = Capacitor [package=cap-pth-small2]
  LED1 = LED - 5mm [color="Red (633nm)" part_number=powerLed package="5 mm [THT]"]
  R1 = Resistor [tolerance=±5% resistance=220 package=THT]
  Power_plug1 = Power plug
  LED2 = LED - 5mm [color="Blue (470nm)" part_number=activityLed package="5 mm [THT]"]
  R2 = Resistor [tolerance=±5% resistance=220 package=THT]
  Part1 = Bluetooth HC-05 Macho
  U2 = WS2801 [package=sop-14]

nets:
  GND: C2.1, U1.GND, C1.1, LED1.cathode, Power_plug1.GND, LED2.cathode, Part1.GND, U2.GND
  N1: C2.2, U1.XLAT2, XTAL1.pin_1
  N2: U1.D2, Part1.TXD
  N3: U1.D3_(PWM), Part1.RXD
  N4: U1.D4, Part1.VCC
  5V: U1.VCC, U1.AVCC, U1.AREF, R1.Pin_0, Power_plug1.VCC
  N5: U1.XLAT1, XTAL1.pin_0, C1.2
  N6: U1.D5_(PWM), Part1.State
  N7: U1.D6_(PWM), R2.Pin_0
  N8: U1.D11_(PWM), U2.SDI
  N9: U1.D13, U2.CKI
  N10: LED1.anode, R1.Pin_1
  N11: LED2.anode, R2.Pin_1
